# Fritzing sketch breadboard-step-1 (saved by Fritzing 0.9.4)
breadboards: 1

parts:
  LED3 = LED - 3mm [color="White (4500K)" package="3 mm [THT]"]
  R2 = Resistor [tolerance=±5% resistance=220 package=THT]
  C5 = Ceramic Capacitor [capacitance=100nF package="200 mil [THT, multilayer]"]
  U2 = atmega328 [package=dip]

nets:
  N1: LED3.cathode, U2.GND
  N2: LED3.anode, R2.Pin_1
  N3: R2.Pin_0, U2.D8
  N4: C5.1, U2.RESET
  N5: U2.VCC, U2.AVCC, U2.AREF

notes:
  Black = GND
  Red = VCC
  Yellow = TX
  White = RX
  Blue = DTR
