# Fritzing sketch breadboard-step-2 (saved by Fritzing 0.9.4)
breadboards: 1

parts:
  C5 = Ceramic Capacitor [capacitance=100nF package="200 mil [THT, multilayer]"]
  Part1 = NRF24L01+ Breakout Board
  U2 = atmega328 [package=dip]

nets:
  N1: C5.1, U2.RESET
  GND: Part1.GND, U2.GND
  VCC: Part1.VCC, U2.VCC, U2.AVCC, U2.AREF
  N2: Part1.CE, U2.D10_(PWM)
  N3: Part1.CS, U2.D9_(PWM)
  N4: Part1.SCK, U2.D13
  N5: Part1.MOSI, U2.D11_(PWM)
  N6: Part1.MISO, U2.D12

notes:
  USB to TTL
  Black = GND
  Red = VCC
  Yellow = TX
  White = RX
  Blue = DTR
