# Fritzing sketch breadboard-step-4 (saved by Fritzing 0.9.4)
breadboards: 1

parts:
  C5 = Ceramic Capacitor [capacitance=100nF package="200 mil [THT, multilayer]"]
  Part1 = NRF24L01+ Breakout Board
  ZS-042_RTC1 = ZS-042 RTC Module
  R3 = Resistor [tolerance=±5% resistance=1k package=THT]
  Q2 = NPN-Transistor [part_number=2N3904 package="TO92 [THT]"]
  RHT1 = Humidity and Temperature Sensor RHT03
  R4 = Resistor [tolerance=±5% resistance=10k package=THT]
  U1 = atmega328 [package=dip]
  Part4 = Soil Moisture Sensor

nets:
  N1: C5.1, U1.RESET
  GND: Part1.GND, ZS-042_RTC1.GND, Q2.C, U1.GND
  VCC: Part1.VCC, ZS-042_RTC1.VCC, RHT1.Vcc, R4.Pin_0, U1.VCC, U1.AVCC, U1.AREF, Part4.VCC
  N2: Part1.CE, U1.D10_(PWM)
  N3: Part1.CS, U1.D9_(PWM)
  N4: Part1.SCK, U1.D13
  N5: Part1.MOSI, U1.D11_(PWM)
  N6: Part1.MISO, U1.D12
  N7: ZS-042_RTC1.SDA, U1.A4
  N8: ZS-042_RTC1.SCL, U1.A5
  N9: ZS-042_RTC1.SQW, U1.D2
  N10: R3.Pin_0, U1.D4
  N11: R3.Pin_1, Q2.B
  N12: Q2.E, RHT1.GND_2, Part4.GND
  N13: RHT1.Data-signal, R4.Pin_1, U1.D5_(PWM)
  N14: U1.A0, Part4.SIG

notes:
  USB to TTL
  Black = GND
  Red = VCC
  Yellow = TX
  White = RX
  Blue = DTR
