# Fritzing sketch humidity-1 (saved by Fritzing 0.9.3b)
circuit board: 8.46667cm x 5.64444cm
breadboards: 1

parts:
  VCC1 = Battery
  U1 = atmega328 [package=dip]
  Q1 = NPN-Transistor [package="TO92 [THT]"]
  R2 = Resistor [tolerance=±5% resistance=1k package="2512 [SMD]"]
  U2 = V_REG_LD1117VXX [package=78xxl]
  C1 = Electrolytic Capacitor [capacitance=100nF package="100 mil [THT, electrolytic]"]
  C2 = Electrolytic Capacitor [capacitance=10µF package="100 mil [THT, electrolytic]"]
  RHT1 = Humidity and Temperature Sensor RHT03
  Part1 = NRF24L01+ Breakout Board
  R3 = Resistor [tolerance=±5% resistance=47k package=THT]
  ZS-042_RTC1 = ZS-042 RTC Module

nets:
  GND: VCC1.-, U1.GND, Q1.C, U2.GND, C1.-, C2.-, Part1.GND, ZS-042_RTC1.GND
  N1: VCC1.+, U2.IN, C1.+
  N2: U1.D2, ZS-042_RTC1.SQW
  N3: U1.D4, R2.Pin_1
  VCC: U1.VCC, U1.AVCC, U1.AREF, U2.OUT, C2.+, RHT1.Vcc, Part1.VCC, R3.Pin_0, ZS-042_RTC1.VCC
  N4: U1.D5_(PWM), RHT1.Data-signal, R3.Pin_1
  N5: U1.D9_(PWM), Part1.CS
  N6: U1.D10_(PWM), Part1.CE
  N7: U1.D11_(PWM), Part1.MOSI
  N8: U1.D12, Part1.MISO
  N9: U1.D13, Part1.SCK
  N10: U1.A4, ZS-042_RTC1.SDA
  N11: U1.A5, ZS-042_RTC1.SCL
  N12: Q1.E, RHT1.GND_2
  N13: Q1.B, R2.Pin_0
