# Fritzing sketch humidity-arduino-1 (saved by Fritzing 0.9.3b)
breadboards: 1

parts:
  Q1 = NPN-Transistor [package="TO92 [THT]"]
  R2 = Resistor [tolerance=±5% resistance=1k package="2512 [SMD]"]
  RHT1 = Humidity and Temperature Sensor RHT03
  Part1 = NRF24L01+ Breakout Board
  R3 = Resistor [tolerance=±5% resistance=47k package=THT]
  ZS-042_RTC1 = ZS-042 RTC Module
  Part2 = Arduino Uno (Rev3)

nets:
  N1: Q1.E, RHT1.GND_2
  N2: Q1.B, R2.Pin_0
  GND: Q1.C, Part1.GND, ZS-042_RTC1.GND, Part2.GND
  N3: R2.Pin_1, Part2.D4
  VCC: RHT1.Vcc, Part1.VCC, R3.Pin_0, ZS-042_RTC1.VCC, Part2.3V3
  N4: RHT1.Data-signal, R3.Pin_1, Part2.D5_PWM
  N5: Part1.CE, Part2.D10_PWM/SS
  N6: Part1.CS, Part2.D9_PWM
  N7: Part1.SCK, Part2.D13/SCK
  N8: Part1.MOSI, Part2.D11_PWM/MOSI
  N9: Part1.MISO, Part2.D12/MISO
  N10: ZS-042_RTC1.SDA, Part2.A4/SDA
  N11: ZS-042_RTC1.SCL, Part2.A5/SCL
  N12: ZS-042_RTC1.SQW, Part2.D2
