# Fritzing sketch nano-nrf24-2xds18b20 (saved by Fritzing 0.9.4)
breadboards: 1

parts:
  Part1 = Arduino Nano (Rev3.0)
  Part3 = NRF24L01+ Breakout Board
  DS1 = DS18B20 1-Wire Temperature Sensor [part_number=DS18B20]
  DS2 = DS18B20 1-Wire Temperature Sensor [part_number=DS18B20]
  R2 = Resistor [tolerance=±5% resistance=4.7k package="0805 [SMD]"]
  R3 = Resistor [tolerance=±5% resistance=4.7k package="0805 [SMD]"]

nets:
  GND: Part1.GND, Part3.GND, DS1.GND, DS2.GND
  N1: Part1.D2, R2.Pin_0
  N2: Part1.D3, R3.Pin_0
  N3: Part1.D9, Part3.CS
  N4: Part1.D10, Part3.CE
  N5: Part1.D11/MOSI, Part3.MOSI
  N6: Part1.D12/MISO, Part3.MISO
  VDD: Part1.3V3, Part3.VCC, DS1.DQ, DS1.VDD, DS2.DQ, DS2.VDD, R2.Pin_1, R3.Pin_1
  N7: Part1.D13/SCK, Part3.SCK

notes:
  https://lastminuteengineers.com/ds18b20-arduino-tutorial/
