# Fritzing sketch nano-nrf24-2xmoisture (saved by Fritzing 0.9.4)
breadboards: 1

parts:
  Part1 = Arduino Nano (Rev3.0)
  Part3 = NRF24L01+ Breakout Board
  Part4 = Soil Moisture Sensor
  Part5 = Soil Moisture Sensor

nets:
  GND: Part1.GND, Part3.GND, Part4.GND, Part5.GND
  N1: Part1.D9, Part3.CS
  N2: Part1.D10, Part3.CE
  N3: Part1.D11/MOSI, Part3.MOSI
  N4: Part1.D12/MISO, Part3.MISO
  N5: Part1.A1, Part5.SIG
  N6: Part1.A0, Part4.SIG
  VCC: Part1.3V3, Part3.VCC, Part4.VCC, Part5.VCC
  N7: Part1.D13/SCK, Part3.SCK
