# Fritzing sketch nrf24-low-power-humidity-moisture (saved by Fritzing 0.9.4)
breadboards: 1

parts:
  Part1 = NRF24L01+ Breakout Board
  ZS-042_RTC1 = ZS-042 RTC Module
  R3 = Resistor [tolerance=±5% resistance=1k package=THT]
  Q2 = NPN-Transistor [part_number=2N3904 package="TO92 [THT]"]
  RHT1 = Humidity and Temperature Sensor RHT03
  R4 = Resistor [tolerance=±5% resistance=10k package=THT]
  U1 = atmega328 [package=dip]
  Part4 = Soil Moisture Sensor
  R5 = Resistor [tolerance=±5% resistance=1k package=THT]
  R6 = Resistor [tolerance=±5% resistance=1k package=THT]
  VCC1 = Battery

nets:
  GND: Part1.GND, ZS-042_RTC1.GND, Q2.C, U1.GND, VCC1.-
  VCC: Part1.VCC, ZS-042_RTC1.VCC, RHT1.Vcc, R4.Pin_0, U1.VCC, U1.AVCC, U1.AREF, Part4.VCC
  N1: Part1.CE, U1.D10_(PWM)
  N2: Part1.CS, U1.D9_(PWM)
  N3: Part1.SCK, U1.D13
  N4: Part1.MOSI, U1.D11_(PWM)
  N5: Part1.MISO, U1.D12
  N6: ZS-042_RTC1.SDA, U1.A4
  N7: ZS-042_RTC1.SCL, U1.A5
  N8: ZS-042_RTC1.SQW, U1.D2
  N9: R3.Pin_0, U1.D4
  N10: R3.Pin_1, Q2.B
  N11: Q2.E, RHT1.GND_2, Part4.GND, R6.Pin_1
  N12: RHT1.Data-signal, R4.Pin_1, U1.D5_(PWM)
  N13: U1.A0, Part4.SIG
  N14: U1.A1, R5.Pin_1, R6.Pin_0
  N15: R5.Pin_0, VCC1.+
